# Fritzing sketch WiringDiagram (saved by Fritzing 0.9.3b)
breadboards: 1

parts:
  J1 = Infrared Proximity Sensor
  Raspberry_Pi_1 = Raspberry Pi 3 [part_number=RPI-3-V1.2]
  J2 = Basic Servo
  J3 = Basic Servo
  J4 = Infrared Proximity Sensor
  LED1 = smd LED [color="Red (633nm)" package="1206 [SMD]"]
  LED2 = smd LED [color="Red (633nm)" package="1206 [SMD]"]
  R1 = Resistor [tolerance=±5% resistance=220 package="0603 [SMD]"]
  R2 = Resistor [tolerance=±5% resistance=220 package="0603 [SMD]"]
  Part1 = 16-Channel 12-bit PCA9685 PWM/Servo Driver

nets:
  N1: J1.Vout, Raspberry_Pi_1.GIPO19, R1.Pin_0
  GND: J1.GND, Raspberry_Pi_1.GND, J2.pulse, J3.pulse, J4.GND, LED1.anode, LED2.anode, Part1.GND
  VCC: J1.Vcc, Raspberry_Pi_1.5V, J2.vcc, J3.vcc, J4.Vcc, Part1.V+
  3V3: Raspberry_Pi_1.3v3, Part1.VCC
  N2: Raspberry_Pi_1.GPIO2, Part1.SDA
  N3: Raspberry_Pi_1.GPIO3, Part1.SCL
  N4: Raspberry_Pi_1.GIPO26, J4.Vout, R2.Pin_0
  N5: J2.gnd, Part1.2
  N6: J3.gnd, Part1.3
  N7: LED1.cathode, R1.Pin_1
  N8: LED2.cathode, R2.Pin_1

notes:
  Internal Motion Sensor

custom parts:
  16-Channel 12-bit PCA9685 PWM/Servo Driver: The Adafruit 16-Channel 12-bit PWM/Servo Driver will drive up to 16 servos over I2C with only 2 pins. The on-board PCA9685 PWM controller will drive all 16 channels simultaneously with no additional processing overhead. What's more, you can chain up to 62 of them to control up to 992 servos - all with the same 2 pins
